# Fritzing sketch Curcuit Sketch (saved by Fritzing 0.9.2b)
breadboards: 1

parts:
  U1 = LCD-16X2 [package=lcd-16x2]
  Part1 = Arduino Mega ADK (Rev3)
  R1 = Resistor [tolerance=±5% resistance=033 package=THT]

nets:
  VSS: U1.VSS, U1.R_W, U1.K, Part1.GND, R1.Pin_0
  VDD: U1.VDD, U1.A, Part1.5V
  N1: U1.VO, R1.Pin_1
  N2: U1.RS, Part1.D12_PWM
  N3: U1.E, Part1.D11_PWM
  N4: U1.DB4, Part1.D2_PWM
  N5: U1.DB5, Part1.D3_PWM
  N6: U1.DB6, Part1.D4_PWM
  N7: U1.DB7, Part1.D5_PWM

notes:
  Resistor 3.3kOhm
